// Logisim project Lab 2.circ as structural Verilog
module Task_1 (
  input  A,
  input  A_2,
  input  B,
  input  A_3,
  input  B_2,
  input  A_4,
  input  B_3,
  output A_prime,
  output AB,
  output A_prime_B_prime___A_B,
  output A_B__prime
);

  wire nand_2_out, nand_3_out, nand_4_out, nand_5_out, nand_6_out, nand_9_out;

  nand nand_1 (A_prime, A, A);
  nand nand_2 (nand_2_out, A_2, B);
  nand nand_3 (nand_3_out, A_3, A_3);
  nand nand_4 (nand_4_out, B_2, B_2);
  nand nand_5 (nand_5_out, A_4, A_4);
  nand nand_6 (nand_6_out, B_3, B_3);
  nand nand_7 (AB, nand_2_out, nand_2_out);
  nand nand_8 (A_prime_B_prime___A_B, nand_3_out, nand_4_out);
  nand nand_9 (nand_9_out, nand_5_out, nand_6_out);
  nand nand_10 (A_B__prime, nand_9_out, nand_9_out);

  // Notes on the sheet:
  //   (AB)'
  //   A'
  //   B'
  //   A'
  //   B'
  //   (A'B')"=A+B
endmodule

module Task_2 (
  input  A,
  input  B,
  input  A_2,
  input  B_2,
  input  A_3,
  input  B_3,
  input  A_4,
  input  B_4,
  output out_9,
  output AB__A_B__prime__prime,
  output out_11,
  output out_12
);

  wire nand_1_out, nand_2_out, nand_3_out, nand_4_out, nand_5_out, nand_6_out, nand_8_out, nor_1_out,
       nor_2_out, nor_3_out, nor_4_out, nor_5_out, nor_6_out, nor_7_out;

  nand nand_1 (nand_1_out, A, B);
  nand nand_2 (nand_2_out, A_3, B_3);
  nor nor_1 (nor_1_out, A_4, B_4);
  nand nand_3 (nand_3_out, A, nand_1_out);
  nand nand_4 (nand_4_out, nand_1_out, B);
  nor nor_2 (nor_2_out, A_2, A_2);
  nor nor_3 (nor_3_out, B_2, B_2);
  nor nor_4 (nor_4_out, B_2, A_2);
  nand nand_5 (nand_5_out, A_3, nand_2_out);
  nand nand_6 (nand_6_out, nand_2_out, B_3);
  nor nor_5 (nor_5_out, A_4, nor_1_out);
  nor nor_6 (nor_6_out, nor_1_out, B_4);
  nand nand_7 (out_9, nand_3_out, nand_4_out);
  nor nor_7 (nor_7_out, nor_2_out, nor_3_out);
  nand nand_8 (nand_8_out, nand_5_out, nand_6_out);
  nor nor_8 (out_12, nor_5_out, nor_6_out);
  nor nor_9 (AB__A_B__prime__prime, nor_7_out, nor_4_out);
  nand nand_9 (out_11, nand_8_out, nand_8_out);

  // Notes on the sheet:
  //   XOR Using NAND
  //   XOR Using Nor
  //   XNOR Using NAND
  //   XNOR Using XOR
  //   (AB)'
  //   (AB)'
  //   (A+B)'
  //   (A.(AB)')'=A'+AB
  //   (A+A)'=A'
  //   (B+B)'=B'
  //   (A+B)'
  //   (A.(AB)')'
  //   (A+(A+B)')'
  //   (B.(AB)')'=B'+AB
  //   (B.(AB)')'
  //   (B+(A+B)')'
  //   ((A'+AB).(B'+AB))'
  //   ((A(AB)')'.(B(AB)')')'
  //   ((A+(A+B)')'+(B+(A+B)')')'
  //   (A'+B')' = AB
  //   (A(AB)')'.(B(AB)')'
endmodule

module Task_3 (
  input  A,
  input  B,
  input  C,
  output AC_BC_prime
);

  wire ic7404_1_a_prime_3, ic7408_1_ab_3, ic7408_1_ab_4;

  ic7404 ic7404_1 (.A_3(C), .A_prime_3(ic7404_1_a_prime_3));  // open: A, A_prime, A_2, A_prime_2, A_4, A_prime_4
  ic7408 ic7408_1 (
    .A_3(ic7404_1_a_prime_3), .AB_3(ic7408_1_ab_3), .B_3(B), .A_4(C), .AB_4(ic7408_1_ab_4), .B_4(A));  // open: A, AB, B, A_2, AB_2, B_2
  ic7432 ic7432_1 (
    .A_4(ic7408_1_ab_3), .A_prime_B_prime___A_B_4(AC_BC_prime), .B_4(ic7408_1_ab_4));  // open: A, A_prime_B_prime___A_B, B, A_2, A_prime_B_prime___A_B_2, B_2, A_3, A_prime_B_prime___A_B_3, B_3

  // Notes on the sheet:
  //   C'
  //   AC
  //   BC'
endmodule

module ic7408 (
  input  A,
  input  B,
  input  A_2,
  input  B_2,
  input  A_3,
  input  B_3,
  input  A_4,
  input  B_4,
  output AB,
  output AB_2,
  output AB_3,
  output AB_4
);

  wire nand_1_out, nand_2_out, nand_3_out, nand_4_out;

  nand nand_1 (nand_1_out, A, B);
  nand nand_2 (nand_2_out, A_2, B_2);
  nand nand_3 (nand_3_out, A_3, B_3);
  nand nand_4 (nand_4_out, A_4, B_4);
  nand nand_5 (AB, nand_1_out, nand_1_out);
  nand nand_6 (AB_2, nand_2_out, nand_2_out);
  nand nand_7 (AB_3, nand_3_out, nand_3_out);
  nand nand_8 (AB_4, nand_4_out, nand_4_out);

  // Notes on the sheet:
  //   (AB)'
  //   (AB)'
  //   (AB)'
  //   (AB)'
endmodule

module ic7432 (
  input  A,
  input  B,
  input  A_2,
  input  B_2,
  input  A_3,
  input  B_3,
  input  A_4,
  input  B_4,
  output A_prime_B_prime___A_B,
  output A_prime_B_prime___A_B_2,
  output A_prime_B_prime___A_B_3,
  output A_prime_B_prime___A_B_4
);

  wire nand_1_out, nand_2_out, nand_3_out, nand_4_out, nand_5_out, nand_6_out, nand_7_out, nand_8_out;

  nand nand_1 (nand_1_out, A, A);
  nand nand_2 (nand_2_out, B, B);
  nand nand_3 (nand_3_out, A_2, A_2);
  nand nand_4 (nand_4_out, B_2, B_2);
  nand nand_5 (nand_5_out, A_3, A_3);
  nand nand_6 (nand_6_out, B_3, B_3);
  nand nand_7 (nand_7_out, A_4, A_4);
  nand nand_8 (nand_8_out, B_4, B_4);
  nand nand_9 (A_prime_B_prime___A_B, nand_1_out, nand_2_out);
  nand nand_10 (A_prime_B_prime___A_B_2, nand_3_out, nand_4_out);
  nand nand_11 (A_prime_B_prime___A_B_3, nand_5_out, nand_6_out);
  nand nand_12 (A_prime_B_prime___A_B_4, nand_7_out, nand_8_out);

  // Notes on the sheet:
  //   A'
  //   B'
  //   A'
  //   B'
  //   A'
  //   B'
  //   A'
  //   B'
endmodule

module ic7404 (
  input  A,
  input  A_2,
  input  A_3,
  input  A_4,
  output A_prime,
  output A_prime_2,
  output A_prime_3,
  output A_prime_4
);

  nand nand_1 (A_prime, A, A);
  nand nand_2 (A_prime_2, A_2, A_2);
  nand nand_3 (A_prime_3, A_3, A_3);
  nand nand_4 (A_prime_4, A_4, A_4);
endmodule
