// Logisim project Lab 3.circ as structural Verilog
module ic7404 (
  input  in_1,
  input  in_2,
  input  in_3,
  input  in_4,
  output out_5,
  output out_6,
  output out_7,
  output out_8
);

  not not_1 (out_5, in_1);
  not not_2 (out_6, in_2);
  not not_3 (out_7, in_3);
  not not_4 (out_8, in_4);
endmodule

module ic7408 (
  input  in_1,
  input  in_2,
  input  in_3,
  input  in_4,
  input  in_5,
  input  in_6,
  input  in_7,
  input  in_8,
  input  in_9,
  output out_10,
  output out_11,
  output out_12
);

  and and_1 (out_10, in_1, in_2, in_3);
  and and_2 (out_11, in_4, in_5, in_6);
  and and_3 (out_12, in_7, in_8, in_9);
endmodule

module ic_7432 (
  input  in_1,
  input  in_2,
  input  in_3,
  input  in_4,
  input  in_5,
  input  in_6,
  input  in_7,
  input  in_8,
  input  in_9,
  output out_10,
  output out_11,
  output out_12
);

  or or_1 (out_10, in_1, in_2, in_3);
  or or_2 (out_11, in_4, in_5, in_6);
  or or_3 (out_12, in_7, in_8, in_9);
endmodule

module _1st_Canonical_Form (
  input  A,
  input  B,
  input  C
);

  wire ic7404_1_out_5, ic7404_1_out_6, ic7404_1_out_8, ic7408_1_out_10, ic7408_1_out_11, ic7408_1_out_12,
       ic_7432_1_out_10;

  ic7404 ic7404_1 (
    .in_1(A), .in_2(C), .in_4(B), .out_5(ic7404_1_out_5), .out_6(ic7404_1_out_6), .out_8(ic7404_1_out_8));  // open: in_3, out_7
  ic7408 ic7408_1 (
    .in_1(ic7404_1_out_5), .in_2(ic7404_1_out_8), .in_3(C), .in_4(A), .in_5(B), .in_6(ic7404_1_out_6),
    .in_7(ic7404_1_out_6), .in_8(B), .in_9(ic7404_1_out_5), .out_10(ic7408_1_out_10),
    .out_11(ic7408_1_out_11), .out_12(ic7408_1_out_12));
  ic_7432 ic_7432_1 (
    .in_1(ic7408_1_out_10), .in_2(ic7408_1_out_12), .in_3(ic7408_1_out_11), .out_10(ic_7432_1_out_10));  // open: in_4, in_5, in_6, in_7, in_8, in_9, out_11, out_12

  // Notes on the sheet:
  //   A'
  //   B'
  //   C'
  //   A'BC'
  //   A'B'C
  //   ABC'
  //   A'B'C+A'BC'+ABC'
endmodule

module _2nd_Canonical_Form (
  input  A,
  input  B,
  input  C
);

  wire ic7404_1_out_5, ic7404_1_out_6, ic7404_1_out_7, ic7408_1_out_10, ic7408_1_out_12, ic_7432_1_out_10,
       ic_7432_1_out_12, ic_7432_2_out_10, ic_7432_2_out_11, ic_7432_2_out_12;

  ic7404 ic7404_1 (
    .in_1(A), .in_2(B), .in_3(C), .out_5(ic7404_1_out_5), .out_6(ic7404_1_out_6), .out_7(ic7404_1_out_7));  // open: in_4, out_8
  ic_7432 ic_7432_1 (
    .in_1(ic7404_1_out_5), .in_2(B), .in_3(ic7404_1_out_7), .in_7(ic7404_1_out_5), .in_8(ic7404_1_out_6),
    .in_9(ic7404_1_out_7), .out_10(ic_7432_1_out_10), .out_12(ic_7432_1_out_12));  // open: in_4, in_5, in_6, out_11
  ic_7432 ic_7432_2 (
    .in_1(B), .in_2(B), .in_3(C), .in_4(A), .in_5(ic7404_1_out_6), .in_6(ic7404_1_out_7),
    .in_7(ic7404_1_out_5), .in_8(B), .in_9(C), .out_10(ic_7432_2_out_10), .out_11(ic_7432_2_out_11),
    .out_12(ic_7432_2_out_12));
  ic7408 ic7408_1 (
    .in_1(ic_7432_2_out_12), .in_2(ic_7432_2_out_11), .in_3(ic_7432_2_out_10), .in_7(ic_7432_1_out_12),
    .in_8(ic_7432_1_out_10), .in_9(ic7408_1_out_10), .out_10(ic7408_1_out_10), .out_12(ic7408_1_out_12));  // open: in_4, in_5, in_6, out_11

  // Notes on the sheet:
  //   C'
  //   B'
  //   A'
  //   A'+B'+C'
  //   A'+B+C'
  //   A+B+C
  //   A+B'+C'
  //   A'+B+C
  //   (A+B+C)(A+B'+C')(A'+B+C)(A'+B+C')(A'+B'+C')
endmodule
