// Logisim project Lab 4.circ as structural Verilog: 4 circuits, main circuit main
module main (
  input  W,
  input  X,
  input  Y,
  input  Z,
  output A_W_XZ_XY,
  output B_X_prime_Z_X_prime_Y_XY_prime_Z_prime,
  output C_Y_prime_Z_prime_YZ,
  output D_Z_prime
);

  wire ic7404_1_out_5, ic7404_1_out_6, ic7408_1_out_9, ic7408_1_out_10, ic7408_1_out_11, ic7408_1_out_12,
       ic7408_2_out_9, ic7408_2_out_10, ic7408_2_out_11, ic7408_2_out_12, ic7432_1_out_9, ic7432_1_out_11;

  ic7404 ic7404_1 (
    .in_1(X), .in_2(Y), .in_4(Z), .out_5(ic7404_1_out_5), .out_6(ic7404_1_out_6), .out_8(D_Z_prime));  // open: in_3, out_7
  ic7408 ic7408_1 (
    .in_1(ic7404_1_out_5), .in_2(Z), .in_3(ic7404_1_out_5), .in_4(Y), .in_5(X), .in_6(Y), .in_7(Z), .in_8(X),
    .out_9(ic7408_1_out_9), .out_10(ic7408_1_out_10), .out_11(ic7408_1_out_11), .out_12(ic7408_1_out_12));
  ic7408 ic7408_2 (
    .in_1(ic7404_1_out_6), .in_2(D_Z_prime), .in_3(Y), .in_4(Z), .in_5(X), .in_6(ic7404_1_out_6),
    .in_7(ic7408_2_out_11), .in_8(D_Z_prime), .out_9(ic7408_2_out_9), .out_10(ic7408_2_out_10),
    .out_11(ic7408_2_out_11), .out_12(ic7408_2_out_12));
  ic7432 ic7432_1 (
    .in_1(ic7408_1_out_10), .in_2(ic7408_1_out_9), .in_3(ic7432_1_out_9), .in_4(ic7408_2_out_12), .in_5(W),
    .in_6(ic7408_1_out_12), .in_7(ic7432_1_out_11), .in_8(ic7408_1_out_11), .out_9(ic7432_1_out_9),
    .out_10(B_X_prime_Z_X_prime_Y_XY_prime_Z_prime), .out_11(ic7432_1_out_11), .out_12(A_W_XZ_XY));
  ic7432 ic7432_2 (
    .in_7(ic7408_2_out_9), .in_8(ic7408_2_out_10), .out_12(C_Y_prime_Z_prime_YZ));  // open: in_1, in_2, in_3, in_4, in_5, in_6, out_9, out_10, out_11

  // Notes on the sheet:
  //   Z'
  //   X'
  //   Y'
  //   XZ
  //   XY
  //   X'Z
  //   XY'Z'
  //   YZ
  //   Y'Z'
  //   X'Y
endmodule

module ic7432 (
  input  in_1,
  input  in_2,
  input  in_3,
  input  in_4,
  input  in_5,
  input  in_6,
  input  in_7,
  input  in_8,
  output out_9,
  output out_10,
  output out_11,
  output out_12
);

  or or_1 (out_9, in_1, in_2);
  or or_2 (out_10, in_3, in_4);
  or or_3 (out_11, in_5, in_6);
  or or_4 (out_12, in_7, in_8);
endmodule

module ic7408 (
  input  in_1,
  input  in_2,
  input  in_3,
  input  in_4,
  input  in_5,
  input  in_6,
  input  in_7,
  input  in_8,
  output out_9,
  output out_10,
  output out_11,
  output out_12
);

  and and_1 (out_9, in_1, in_2);
  and and_2 (out_10, in_3, in_4);
  and and_3 (out_11, in_5, in_6);
  and and_4 (out_12, in_7, in_8);
endmodule

module ic7404 (
  input  in_1,
  input  in_2,
  input  in_3,
  input  in_4,
  output out_5,
  output out_6,
  output out_7,
  output out_8
);

  not not_1 (out_5, in_1);
  not not_2 (out_6, in_2);
  not not_3 (out_7, in_3);
  not not_4 (out_8, in_4);
endmodule
