// Logisim project Lab 7.circ as structural Verilog: 8 circuits, main circuit main
module main (
  input  D,
  input  C,
  input  B,
  input  in_4,
  input  A
);

  wire a_1_out_5, b_1_out_5, c_1_out_5, d_1_out_5, e_1_e_ba_prime_c_prime_a_prime, f_1_out_5, g_1_out_5;

  a a_1 (.D(D), .C(C), .B(B), .A(A), .out_5(a_1_out_5));
  b b_1 (.D(D), .C(C), .B(B), .A(A), .out_5(b_1_out_5));
  c c_1 (.D(D), .C(C), .B(B), .A(A), .out_5(c_1_out_5));
  d d_1 (.D(D), .C(C), .B(B), .A(A), .out_5(d_1_out_5));
  e e_1 (.D(D), .C(C), .B(B), .A(A), .e_BA_prime_C_prime_A_prime(e_1_e_ba_prime_c_prime_a_prime));
  f f_1 (.D(D), .C(C), .B(B), .A(A), .out_5(f_1_out_5));
  g g_1 (.D(D), .C(C), .B(B), .A(A), .out_5(g_1_out_5));
  _7_Segment_Display u_7_segment_display_1 (
    .g(g_1_out_5), .f(f_1_out_5), .a(a_1_out_5), .b(b_1_out_5), .e(e_1_e_ba_prime_c_prime_a_prime),
    .d(d_1_out_5), .c(c_1_out_5), .dp(in_4));
endmodule

module a (
  input  D,
  input  C,
  input  B,
  input  A,
  output out_5
);

  wire and_1_out, and_2_out, not_1_out, not_2_out;

  not not_1 (not_1_out, C);
  not not_2 (not_2_out, A);
  and and_1 (and_1_out, C, A);
  and and_2 (and_2_out, not_1_out, not_2_out);
  or or_1 (out_5, D, and_1_out, B, and_2_out);

  // Notes on the sheet:
  //   C'
  //   A'
  //   AC
  //   A'C'
  //   a = D+B+C'A'+CA
endmodule

module b (
  input  D,
  input  C,
  input  B,
  input  A,
  output out_5
);

  wire and_1_out, and_2_out, not_1_out, not_2_out, not_3_out;

  not not_1 (not_1_out, C);
  not not_2 (not_2_out, B);
  not not_3 (not_3_out, A);
  and and_1 (and_1_out, A, B);
  and and_2 (and_2_out, not_2_out, not_3_out);
  or or_1 (out_5, D, not_1_out, and_1_out, and_2_out);

  // Notes on the sheet:
  //   C'
  //   B'
  //   A'
  //   BA
  //   B'A'
  //   b=D+BA+C'+B'A'
endmodule

module c (
  input  D,
  input  C,
  input  B,
  input  A,
  output out_5
);

  wire not_1_out;

  not not_1 (not_1_out, B);
  or or_1 (out_5, D, C, not_1_out, A);

  // Notes on the sheet:
  //   B'
  //   c=D+C+B'+A
endmodule

module d (
  input  D,
  input  C,
  input  B,
  input  A,
  output out_5
);

  wire and_1_out, and_2_out, and_3_out, and_4_out, not_1_out, not_2_out, not_3_out;

  not not_1 (not_1_out, C);
  not not_2 (not_2_out, B);
  not not_3 (not_3_out, A);
  and and_1 (and_1_out, A, not_2_out, C);
  and and_2 (and_2_out, not_1_out, B);
  and and_3 (and_3_out, not_1_out, not_3_out);
  and and_4 (and_4_out, B, not_3_out);
  or or_1 (out_5, and_1_out, D, and_2_out, and_3_out, and_4_out);

  // Notes on the sheet:
  //   C'B
  //   C'A'
  //   CB'A
  //   BA'
  //   d=D+BA'+C'A'+C'B+CB'A
endmodule

module e (
  input  D,
  input  C,
  input  B,
  input  A,
  output e_BA_prime_C_prime_A_prime
);

  wire and_1_out, and_2_out, not_1_out, not_2_out;

  not not_1 (not_1_out, C);
  not not_2 (not_2_out, A);
  and and_1 (and_1_out, not_2_out, not_1_out);
  and and_2 (and_2_out, B, not_2_out);
  or or_1 (e_BA_prime_C_prime_A_prime, and_1_out, and_2_out);

  // Notes on the sheet:
  //   C'
  //   A'
  //   C'A'
  //   BA'
endmodule

module f (
  input  D,
  input  C,
  input  B,
  input  A,
  output out_5
);

  wire and_1_out, and_2_out, and_3_out, not_1_out, not_2_out;

  not not_1 (not_1_out, B);
  not not_2 (not_2_out, A);
  and and_1 (and_1_out, C, not_1_out);
  and and_2 (and_2_out, C, not_2_out);
  and and_3 (and_3_out, not_1_out, not_2_out);
  or or_1 (out_5, D, and_1_out, and_2_out, and_3_out);

  // Notes on the sheet:
  //   CB'
  //   CA'
  //   B'A'
  //   f=D+CB'+CA'+B'A'
endmodule

module g (
  input  D,
  input  C,
  input  B,
  input  A,
  output out_5
);

  wire and_1_out, and_2_out, and_3_out, not_1_out, not_2_out, not_3_out, not_4_out;

  not not_1 (not_1_out, D);
  not not_2 (not_2_out, C);
  not not_3 (not_3_out, B);
  not not_4 (not_4_out, A);
  and and_1 (and_1_out, not_1_out, not_2_out, B);
  and and_2 (and_2_out, C, not_3_out);
  and and_3 (and_3_out, B, not_4_out);
  or or_1 (out_5, and_1_out, D, and_2_out, and_3_out);

  // Notes on the sheet:
  //   D'C'B
  //   CB'
  //   BA'
  //   g = D+BA'+D'C'B+CB'
endmodule
