// Logisim project Robot Detection.circ as structural Verilog
module minterm (
  input  A,
  input  B,
  input  C,
  input  D,
  output out_5
);

  wire ic7404_1_out_5, ic7404_1_out_6, ic7404_1_out_7, ic7404_1_out_8, ic7404_2_out_5, ic7404_2_out_6,
       ic7404_2_out_7, ic7404_2_out_8, ic7408_1_out_17, ic7408_1_out_18, ic7408_1_out_19, ic7408_1_out_20,
       ic7408_2_out_17, ic7408_2_out_18, ic7408_2_out_19, ic7408_2_out_20, ic7432_1_out_19, ic7432_1_out_20;

  ic7404 ic7404_1 (
    .in_1(B), .in_2(C), .in_3(D), .in_4(A), .out_5(ic7404_1_out_5), .out_6(ic7404_1_out_6),
    .out_7(ic7404_1_out_7), .out_8(ic7404_1_out_8));
  ic7404 ic7404_2 (
    .in_1(B), .in_2(C), .in_3(D), .in_4(A), .out_5(ic7404_2_out_5), .out_6(ic7404_2_out_6),
    .out_7(ic7404_2_out_7), .out_8(ic7404_2_out_8));
  ic7408 ic7408_1 (
    .in_1(ic7404_1_out_8), .in_2(B), .in_3(ic7404_1_out_6), .in_4(D), .in_5(ic7404_1_out_8), .in_6(B),
    .in_7(C), .in_8(ic7404_1_out_7), .in_9(ic7404_1_out_7), .in_10(ic7404_1_out_6), .in_11(B),
    .in_12(ic7404_1_out_8), .in_13(D), .in_14(ic7404_1_out_6), .in_15(ic7404_1_out_5),
    .in_16(ic7404_1_out_8), .out_17(ic7408_1_out_17), .out_18(ic7408_1_out_18), .out_19(ic7408_1_out_19),
    .out_20(ic7408_1_out_20));
  ic7408 ic7408_2 (
    .in_1(A), .in_2(B), .in_3(C), .in_4(D), .in_5(A), .in_6(B), .in_7(C), .in_8(ic7404_2_out_7), .in_9(D),
    .in_10(C), .in_11(ic7404_2_out_5), .in_12(A), .in_13(D), .in_14(ic7404_2_out_6), .in_15(ic7404_2_out_5),
    .in_16(A), .out_17(ic7408_2_out_17), .out_18(ic7408_2_out_18), .out_19(ic7408_2_out_19),
    .out_20(ic7408_2_out_20));
  ic7432 ic7432_1 (
    .in_1(ic7432_1_out_20), .in_2(ic7432_1_out_20), .in_3(ic7432_1_out_19), .in_4(ic7432_1_out_19),
    .in_9(ic7408_1_out_18), .in_10(ic7408_1_out_17), .in_11(ic7408_1_out_20), .in_12(ic7408_1_out_19),
    .in_13(ic7408_2_out_19), .in_14(ic7408_2_out_18), .in_15(ic7408_2_out_17), .in_16(ic7408_2_out_20),
    .out_17(out_5), .out_19(ic7432_1_out_19), .out_20(ic7432_1_out_20));  // open: in_5, in_6, in_7, in_8, out_18

  // Notes on the sheet:
  //   D'
  //   C'
  //   A'
  //   D'
  //   C'
  //   B'
  //   A'
  //   B'
  //   A'BC'D'
  //   A'B'C'D
  //   AB'CD
  //   ABCD'
  //   ABCD
  //   AB'C'D
  //   A'BCD'
  //   A'BC'D
  //   A'B'C'D+A'BC'D'+A'BC'D+A'BCD'+AB'C'D+AB'CD+ABCD'+ABCD
endmodule

module maxterm (
  input  A,
  input  B,
  input  C,
  input  D,
  output out_5
);

  wire ic7404_1_out_5, ic7404_1_out_6, ic7404_1_out_7, ic7404_1_out_8, ic7404_2_out_5, ic7404_2_out_6,
       ic7404_2_out_7, ic7404_2_out_8, ic7408_1_out_19, ic7408_1_out_20, ic7432_1_out_17, ic7432_1_out_18,
       ic7432_1_out_19, ic7432_1_out_20, ic7432_2_out_17, ic7432_2_out_18, ic7432_2_out_19, ic7432_2_out_20;

  ic7404 ic7404_1 (
    .in_1(B), .in_2(C), .in_3(D), .in_4(A), .out_5(ic7404_1_out_5), .out_6(ic7404_1_out_6),
    .out_7(ic7404_1_out_7), .out_8(ic7404_1_out_8));
  ic7404 ic7404_2 (
    .in_1(B), .in_2(C), .in_3(D), .in_4(A), .out_5(ic7404_2_out_5), .out_6(ic7404_2_out_6),
    .out_7(ic7404_2_out_7), .out_8(ic7404_2_out_8));
  ic7432 ic7432_1 (
    .in_1(ic7404_1_out_8), .in_2(ic7404_1_out_5), .in_3(C), .in_4(D), .in_5(ic7404_1_out_8),
    .in_6(ic7404_1_out_5), .in_7(C), .in_8(ic7404_1_out_7), .in_9(D), .in_10(ic7404_1_out_6), .in_11(B),
    .in_12(ic7404_1_out_8), .in_13(D), .in_14(C), .in_15(B), .in_16(ic7404_1_out_8),
    .out_17(ic7432_1_out_17), .out_18(ic7432_1_out_18), .out_19(ic7432_1_out_19), .out_20(ic7432_1_out_20));
  ic7432 ic7432_2 (
    .in_1(A), .in_2(B), .in_3(ic7404_2_out_6), .in_4(ic7404_2_out_7), .in_5(A), .in_6(ic7404_2_out_5),
    .in_7(ic7404_2_out_6), .in_8(ic7404_2_out_7), .in_9(D), .in_10(ic7404_2_out_6), .in_11(B), .in_12(A),
    .in_13(D), .in_14(C), .in_15(B), .in_16(A), .out_17(ic7432_2_out_17), .out_18(ic7432_2_out_18),
    .out_19(ic7432_2_out_19), .out_20(ic7432_2_out_20));
  ic7408 ic7408_1 (
    .in_1(ic7408_1_out_20), .in_2(ic7408_1_out_20), .in_3(ic7408_1_out_19), .in_4(ic7408_1_out_19),
    .in_9(ic7432_1_out_19), .in_10(ic7432_1_out_18), .in_11(ic7432_1_out_17), .in_12(ic7432_1_out_20),
    .in_13(ic7432_2_out_19), .in_14(ic7432_2_out_18), .in_15(ic7432_2_out_17), .in_16(ic7432_2_out_20),
    .out_17(out_5), .out_19(ic7408_1_out_19), .out_20(ic7408_1_out_20));  // open: in_5, in_6, in_7, in_8, out_18

  // Notes on the sheet:
  //   D'
  //   C'
  //   B'
  //   A'
  //   D'
  //   C'
  //   B'
  //   A'
  //   A'+B'+C+D'
  //   A'+B+C'+D
  //   A'+B'+C+D
  //   A'+B+C+D
  //   A+B+C'+D
  //   A+B'+C'+D'
  //   A+B+C'+D'
  //   A+B+C+D
  //   (A+B+C+D) (A+B+C'+D)(A+B+C'+D')(A+B'+C'+D')(A'+B+C+D)(A'+B+C'+D)(A'+B'+C+D)(A'+B'+C+D')
endmodule

module ic7408 (
  input  in_1,
  input  in_2,
  input  in_3,
  input  in_4,
  input  in_5,
  input  in_6,
  input  in_7,
  input  in_8,
  input  in_9,
  input  in_10,
  input  in_11,
  input  in_12,
  input  in_13,
  input  in_14,
  input  in_15,
  input  in_16,
  output out_17,
  output out_18,
  output out_19,
  output out_20
);

  and and_1 (out_17, in_1, in_2, in_3, in_4);
  and and_2 (out_18, in_5, in_6, in_7, in_8);
  and and_3 (out_19, in_9, in_10, in_11, in_12);
  and and_4 (out_20, in_13, in_14, in_15, in_16);
endmodule

module ic7432 (
  input  in_1,
  input  in_2,
  input  in_3,
  input  in_4,
  input  in_5,
  input  in_6,
  input  in_7,
  input  in_8,
  input  in_9,
  input  in_10,
  input  in_11,
  input  in_12,
  input  in_13,
  input  in_14,
  input  in_15,
  input  in_16,
  output out_17,
  output out_18,
  output out_19,
  output out_20
);

  or or_1 (out_17, in_1, in_2, in_3, in_4);
  or or_2 (out_18, in_5, in_6, in_7, in_8);
  or or_3 (out_19, in_9, in_10, in_11, in_12);
  or or_4 (out_20, in_13, in_14, in_15, in_16);
endmodule

module ic7404 (
  input  in_1,
  input  in_2,
  input  in_3,
  input  in_4,
  output out_5,
  output out_6,
  output out_7,
  output out_8
);

  not not_1 (out_5, in_1);
  not not_2 (out_6, in_2);
  not not_3 (out_7, in_3);
  not not_4 (out_8, in_4);
endmodule
